# Fritzing sketch temp_logger (saved by Fritzing 0.9.3b)
breadboards: 2

parts:
  RHT1 = Humidity and Temperature Sensor RHT03
  S1 = Pushbutton [package="[THT]"]
  S2 = Pushbutton [package="[THT]"]
  R1 = Resistor [tolerance=±5% resistance=10k package=THT]
  R2 = Trimmer Potentiometer [maximum_resistance=10kΩ package=THT]
  U1 = LCD-16X2 [package=lcd-16x2]
  R3 = Resistor [tolerance=±5% resistance=220 package=THT]
  Part1 = Arduino Board Ethernet

nets:
  VCC: RHT1.Vcc, S1.Pin_1, S1.Pin_2, R2.leg2, U1.VDD, R3.Pin_1, Part1.A3, Part1.5V
  N1: RHT1.GND_1, Part1.D7
  N2: RHT1.GND_2, S2.Pin_3, S2.Pin_4, R1.Pin_0, R2.leg1, Part1.GND
  N3: S1.Pin_3, S1.Pin_4, R1.Pin_1
  N4: S2.Pin_1, S2.Pin_2, Part1.RESET
  N5: R2.wiper, U1.VO
  N6: U1.VSS, U1.R_W, U1.K
  N7: U1.RS, Part1.D2_PWM
  N8: U1.E, Part1.D3_PWM
  N9: U1.DB4, Part1.D4
  N10: U1.DB5, Part1.D8
  N11: U1.DB6, Part1.D5_PWM
  N12: U1.DB7, Part1.D6_PWM
  N13: U1.A, R3.Pin_0

notes:
  Arduino uno connected below the shild
  sample data
  arduino reset
  DHT22
  AM2302
